// Logisim project Vjezbe1-Zadatak2-Potpuno zbrajalo.circ as structural Verilog: 1 circuit, main circuit main
module main (
  input  A,
  input  B,
  input  Cin,
  output S,
  output C
);

  wire and_1_out, and_2_out, xor_1_out;

  xor xor_1 (xor_1_out, A, B);
  and and_1 (and_1_out, B, A);
  xor xor_2 (S, Cin, xor_1_out);
  and and_2 (and_2_out, Cin, xor_1_out);
  or or_1 (C, and_1_out, and_2_out);
endmodule
