// Logisim project Vjezbe1-Zadatak3-4-bitno zbrajalo.circ as structural Verilog: 1 circuit, main circuit 4-bitno zbrajalo
module _4_bitno_zbrajalo (
  input  A4,
  input  A3,
  input  A2,
  input  A1,
  input  B4,
  input  B3,
  input  B2,
  input  B1,
  output C5,
  output S4,
  output S3,
  output S2,
  output S1
);

  wire and_1_out, and_2_out, and_3_out, and_4_out, and_5_out, and_6_out, and_7_out, and_8_out, or_1_out,
       or_2_out, or_3_out, xor_1_out, xor_3_out, xor_5_out, xor_7_out;

  xor xor_1 (xor_1_out, A1, B1);
  and and_1 (and_1_out, A1, B1);
  xor xor_2 (S1, 1'b0, xor_1_out);
  and and_2 (and_2_out, 1'b0, xor_1_out);
  or or_1 (or_1_out, and_1_out, and_2_out);
  xor xor_3 (xor_3_out, A2, B2);
  and and_3 (and_3_out, A2, B2);
  xor xor_4 (S2, or_1_out, xor_3_out);
  and and_4 (and_4_out, or_1_out, xor_3_out);
  or or_2 (or_2_out, and_3_out, and_4_out);
  xor xor_5 (xor_5_out, A3, B3);
  and and_5 (and_5_out, A3, B3);
  xor xor_6 (S3, or_2_out, xor_5_out);
  and and_6 (and_6_out, or_2_out, xor_5_out);
  or or_3 (or_3_out, and_5_out, and_6_out);
  xor xor_7 (xor_7_out, A4, B4);
  and and_7 (and_7_out, A4, B4);
  xor xor_8 (S4, or_3_out, xor_7_out);
  and and_8 (and_8_out, or_3_out, xor_7_out);
  or or_4 (C5, and_7_out, and_8_out);
endmodule
