// Logisim project Vjezbe1-Zadatak4-Poluzbrajalo pomocu NILI sklopova.circ as structural Verilog: 1 circuit, main circuit main
module main (
  input  A,
  input  B,
  output S,
  output C
);

  wire nor_1_out, nor_2_out, nor_3_out, nor_4_out, nor_5_out;

  nor nor_1 (nor_1_out, B, B);
  nor nor_2 (nor_2_out, A, A);
  nor nor_3 (nor_3_out, A, nor_1_out);
  nor nor_4 (nor_4_out, B, nor_2_out);
  nor nor_5 (nor_5_out, nor_3_out, nor_4_out);
  nor nor_6 (S, nor_5_out, nor_5_out);
  nor nor_7 (C, nor_2_out, nor_1_out);
endmodule
