// Logisim project Vjezbe1-Zadatak5-Potpuno oduzimalo.circ as structural Verilog: 1 circuit, main circuit main
module main (
  input  A,
  input  B,
  input  Cin,
  output S,
  output C
);

  wire and_1_out, nor_1_out, not_1_out, xor_1_out, xor_3_out;

  xor xor_1 (xor_1_out, A, B);
  and and_1 (and_1_out, Cin, B, A);
  nor nor_1 (nor_1_out, Cin, B, A);
  not not_1 (not_1_out, A);
  xor xor_2 (S, xor_1_out, Cin);
  xor xor_3 (xor_3_out, and_1_out, nor_1_out);
  xor xor_4 (C, xor_3_out, not_1_out);
endmodule
