// Logisim project 4-bitno zbrajalo za vjezbe2.circ as structural Verilog: 1 circuit, main circuit 4-bitno zbrajalo
module _4_bitno_zbrajalo (
  input  [3:0] in_1,
  input  [3:0] in_2,
  output C5,
  output [3:0] out_4
);

  wire and_1_out, and_2_out, and_3_out, and_4_out, and_5_out, and_6_out, and_7_out, and_8_out, or_1_out,
       or_2_out, or_3_out, xor_1_out, xor_3_out, xor_5_out, xor_7_out;

  xor xor_1 (xor_1_out, in_1[0], in_2[0]);
  and and_1 (and_1_out, in_1[0], in_2[0]);
  xor xor_2 (out_4[0], 1'b0, xor_1_out);
  and and_2 (and_2_out, 1'b0, xor_1_out);
  or or_1 (or_1_out, and_1_out, and_2_out);
  xor xor_3 (xor_3_out, in_1[1], in_2[1]);
  and and_3 (and_3_out, in_1[1], in_2[1]);
  xor xor_4 (out_4[1], or_1_out, xor_3_out);
  and and_4 (and_4_out, or_1_out, xor_3_out);
  or or_2 (or_2_out, and_3_out, and_4_out);
  xor xor_5 (xor_5_out, in_1[2], in_2[2]);
  and and_5 (and_5_out, in_1[2], in_2[2]);
  xor xor_6 (out_4[2], or_2_out, xor_5_out);
  and and_6 (and_6_out, or_2_out, xor_5_out);
  or or_3 (or_3_out, and_5_out, and_6_out);
  xor xor_7 (xor_7_out, in_1[3], in_2[3]);
  and and_7 (and_7_out, in_1[3], in_2[3]);
  xor xor_8 (out_4[3], or_3_out, xor_7_out);
  and and_8 (and_8_out, or_3_out, xor_7_out);
  or or_4 (C5, and_7_out, and_8_out);
endmodule
