// Logisim project Vjezbe2.circ as structural Verilog: 1 circuit, main circuit ALU
module ALU (
  input  [3:0] A,
  input  [3:0] B,
  input  [2:0] SelOp,
  output [3:0] out_4,
  output [3:0] out_5
);

  wire n4_bitno_zbrajalo_1_c5, subtractor_1_bout;
  wire [3:0] and_1_out, bit_extender_1_out, bit_extender_2_out, divider_1_out, divider_1_rem,
       multiplier_1_cout, multiplier_1_out, n4_bitno_zbrajalo_1_out_4, not_1_out, or_1_out, subtractor_1_out,
       xor_1_out;

  _4_bitno_zbrajalo u_4_bitno_zbrajalo_1 (
    .in_1(A), .in_2(B), .out_4(n4_bitno_zbrajalo_1_out_4), .C5(n4_bitno_zbrajalo_1_c5));
  Subtractor #(.width(4)) subtractor_1 (.a(A), .b(B), .out(subtractor_1_out), .bin(1'b0), .bout(subtractor_1_bout));
  Multiplier #(.width(4)) multiplier_1 (.a(A), .b(B), .out(multiplier_1_out), .cin(4'b0000), .cout(multiplier_1_cout));
  Divider #(.width(4)) divider_1 (.a(A), .b(B), .out(divider_1_out), .upper(4'b0000), .rem(divider_1_rem));
  assign and_1_out = A & B;  // AND_Gate and_1, 4 bits wide
  assign or_1_out = A | B;  // OR_Gate or_1, 4 bits wide
  assign xor_1_out = A ^ B;  // XOR_Gate xor_1, 4 bits wide
  assign not_1_out = ~A;  // NOT_Gate not_1, 4 bits wide
  Multiplexer #(.select(3), .width(4)) multiplexer_1 (
    .in0(n4_bitno_zbrajalo_1_out_4), .in1(subtractor_1_out), .in2(multiplier_1_out), .in3(divider_1_out),
    .in4(and_1_out), .in5(or_1_out), .in6(xor_1_out), .in7(not_1_out), .out(out_5), .sel(SelOp), .en(1'b1));
  assign bit_extender_1_out = {{3{1'b0}}, n4_bitno_zbrajalo_1_c5};  // Bit_Extender bit_extender_1
  assign bit_extender_2_out = {{3{1'b0}}, subtractor_1_bout};  // Bit_Extender bit_extender_2
  Multiplexer #(.select(3), .width(4)) multiplexer_2 (
    .in0(bit_extender_1_out), .in1(bit_extender_2_out), .in2(multiplier_1_cout), .in3(divider_1_rem),
    .in4(4'b0000), .in5(4'b0000), .in6(4'b0000), .in7(4'b0000), .out(out_4), .sel(SelOp), .en(1'b1));
endmodule
