// Logisim project ALU ZA vjezbe4.circ as structural Verilog: 1 circuit, main circuit ALU
module ALU (
  input  [3:0] A,
  input  [3:0] B,
  input  [2:0] SelOp,
  output [3:0] _1__Ulaz_za_2_NBCD,
  output [3:0] _1__Ulaz_za__3__NBCD,
  output _2__Ulaz_za_1__NBCD,
  output _2__Ulaz_za_2__NBCD,
  output _2__Ulaz_za_3__NBCD,
  output [3:0] _1__Ulaz_za_1__NBCD
);

  wire and_2_out, and_3_out, and_4_out, comparator_1_lt, comparator_2_eq, comparator_3_gt, comparator_4_eq,
       comparator_4_lt, comparator_5_eq, multiplexer_5_out, n4_bitno_zbrajalo_1_c5, not_2_out,
       subtractor_1_bout;
  wire [3:0] and_1_out, bit_extender_1_out, bit_extender_2_out, divider_1_out, divider_1_rem,
       multiplexer_1_out, multiplier_1_cout, multiplier_1_out, n4_bitno_zbrajalo_1_out_4, negator_1_out,
       not_1_out, or_1_out, subtractor_1_out, xor_1_out;

  _4_bitno_zbrajalo u_4_bitno_zbrajalo_1 (
    .in_1(A), .in_2(B), .out_4(n4_bitno_zbrajalo_1_out_4), .C5(n4_bitno_zbrajalo_1_c5));
  Subtractor #(.width(4)) subtractor_1 (.a(A), .b(B), .out(subtractor_1_out), .bin(1'b0), .bout(subtractor_1_bout));
  Multiplier #(.width(4)) multiplier_1 (.a(A), .b(B), .out(multiplier_1_out), .cin(4'b0000), .cout(multiplier_1_cout));
  Divider #(.width(4)) divider_1 (.a(A), .b(B), .out(divider_1_out), .upper(4'b0000), .rem(divider_1_rem));
  assign and_1_out = A & B;  // AND_Gate and_1, 4 bits wide
  assign or_1_out = A | B;  // OR_Gate or_1, 4 bits wide
  assign xor_1_out = A ^ B;  // XOR_Gate xor_1, 4 bits wide
  assign not_1_out = ~A;  // NOT_Gate not_1, 4 bits wide
  Multiplexer #(.select(3), .width(4)) multiplexer_1 (
    .in0(n4_bitno_zbrajalo_1_out_4), .in1(subtractor_1_out), .in2(multiplier_1_out), .in3(divider_1_out),
    .in4(and_1_out), .in5(or_1_out), .in6(xor_1_out), .in7(not_1_out), .out(multiplexer_1_out), .sel(SelOp),
    .en(1'b1));
  assign bit_extender_1_out = {{3{1'b0}}, n4_bitno_zbrajalo_1_c5};  // Bit_Extender bit_extender_1
  assign bit_extender_2_out = {{3{1'b0}}, subtractor_1_bout};  // Bit_Extender bit_extender_2
  Multiplexer #(.select(3), .width(4)) multiplexer_2 (
    .in0(bit_extender_1_out), .in1(bit_extender_2_out), .in2(multiplier_1_cout), .in3(divider_1_rem),
    .in4(4'b0000), .in5(4'b0000), .in6(4'b0000), .in7(4'b0000), .out(_1__Ulaz_za__3__NBCD), .sel(SelOp),
    .en(1'b1));
  Comparator #(.width(4), .mode("unsigned")) comparator_1 (.a(A), .b(B), .lt(comparator_1_lt));  // open: gt, eq
  Comparator #(.width(3), .mode("unsigned")) comparator_2 (
    .a(SelOp), .b(3'b001), .eq(comparator_2_eq));  // open: gt, lt
  Comparator #(.width(3), .mode("unsigned")) comparator_3 (
    .a(SelOp), .b(3'b100), .gt(comparator_3_gt));  // open: eq, lt
  Comparator #(.width(3), .mode("unsigned")) comparator_4 (
    .a(SelOp), .b(3'b011), .eq(comparator_4_eq), .lt(comparator_4_lt));  // open: gt
  Comparator #(.width(4)) comparator_5 (.a(B), .b(4'b0000), .eq(comparator_5_eq));  // open: gt, lt
  and and_2 (and_2_out, comparator_4_eq, comparator_5_eq);
  not not_2 (not_2_out, comparator_5_eq);
  and and_3 (and_3_out, comparator_1_lt, comparator_2_eq);
  or or_2 (_2__Ulaz_za_2__NBCD, comparator_3_gt, and_2_out);
  and and_4 (and_4_out, comparator_4_eq, not_2_out);
  Negator #(.width(4)) negator_1 (.in(multiplexer_1_out), .out(negator_1_out));
  Multiplexer #(.width(4)) multiplexer_3 (
    .in0(_1__Ulaz_za__3__NBCD), .in1(4'b0000), .out(_1__Ulaz_za_1__NBCD), .sel(and_4_out));  // open: en
  Multiplexer #(.width(4)) multiplexer_4 (
    .in0(multiplexer_1_out), .in1(negator_1_out), .out(_1__Ulaz_za_2_NBCD), .sel(multiplexer_5_out), .en(1'b1));
  Multiplexer multiplexer_5 (
    .in0(_2__Ulaz_za_1__NBCD), .in1(1'b0), .out(multiplexer_5_out), .sel(comparator_3_gt), .en(1'b1));
  or or_3 (_2__Ulaz_za_1__NBCD, and_3_out, _2__Ulaz_za_2__NBCD);
  or or_4 (_2__Ulaz_za_3__NBCD, _2__Ulaz_za_2__NBCD, comparator_4_lt);
endmodule
