// Logisim project NBCD za vjezbe4.circ as structural Verilog: 1 circuit, main circuit NBCD
module NBCD (
  input  [3:0] in_1,
  input  Kontrola_za_minus_i_greske,
  output [3:0] out_3,
  output [3:0] out_4
);

  wire and_1_out, and_2_out, and_3_out, and_4_out, and_5_out, and_6_out, and_7_out, and_8_out, and_9_out,
       and_10_out, and_11_out, and_12_out, and_13_out, and_14_out, and_15_out, and_16_out, and_17_out,
       and_18_out, and_19_out, and_20_out, and_21_out, and_22_out, and_23_out, and_24_out, and_25_out,
       and_26_out, and_27_out, and_28_out, and_29_out, and_30_out, and_31_out, and_32_out, and_33_out,
       and_34_out, and_35_out, and_36_out, not_1_out, not_2_out, not_3_out, not_4_out, not_5_out, or_1_out,
       or_2_out, or_3_out, or_4_out, or_5_out, or_6_out, or_7_out;

  not not_1 (not_1_out, in_1[3]);
  not not_2 (not_2_out, in_1[2]);
  not not_3 (not_3_out, in_1[0]);
  not not_4 (not_4_out, in_1[1]);
  and and_1 (and_1_out, not_2_out, in_1[1]);
  and and_2 (and_2_out, in_1[1], not_3_out);
  and and_3 (and_3_out, not_1_out, in_1[2], not_4_out);
  and and_4 (and_4_out, in_1[3], not_2_out);
  and and_5 (and_5_out, in_1[3], in_1[0]);
  and and_6 (and_6_out, not_4_out, not_3_out);
  and and_7 (and_7_out, in_1[2], not_3_out);
  and and_8 (and_8_out, not_1_out, in_1[2], not_4_out);
  and and_9 (and_9_out, in_1[3], not_2_out);
  and and_10 (and_10_out, in_1[3], in_1[1]);
  and and_11 (and_11_out, not_2_out, not_3_out);
  and and_12 (and_12_out, not_1_out, in_1[1]);
  and and_13 (and_13_out, not_1_out, in_1[2], in_1[0]);
  and and_14 (and_14_out, in_1[2], in_1[1]);
  and and_15 (and_15_out, in_1[3], not_2_out, not_4_out);
  and and_16 (and_16_out, in_1[3], not_3_out);
  and and_17 (and_17_out, not_1_out, not_2_out);
  and and_18 (and_18_out, not_1_out, not_4_out, not_3_out);
  and and_19 (and_19_out, not_2_out, not_3_out);
  and and_20 (and_20_out, not_1_out, in_1[1], in_1[0]);
  and and_21 (and_21_out, in_1[3], not_4_out, in_1[0]);
  and and_22 (and_22_out, not_2_out, not_3_out);
  and and_23 (and_23_out, in_1[1], not_3_out);
  and and_24 (and_24_out, in_1[3], in_1[2], in_1[0]);
  and and_25 (and_25_out, in_1[3], not_3_out);
  and and_26 (and_26_out, in_1[3], in_1[1]);
  and and_27 (and_27_out, not_1_out, not_2_out, not_3_out);
  and and_28 (and_28_out, not_2_out, in_1[1], in_1[0]);
  and and_29 (and_29_out, in_1[2], not_4_out, in_1[0]);
  and and_30 (and_30_out, in_1[2], in_1[1], not_3_out);
  and and_31 (and_31_out, in_1[3], not_4_out);
  and and_32 (and_32_out, not_1_out, not_4_out);
  and and_33 (and_33_out, not_1_out, in_1[0]);
  and and_34 (and_34_out, not_4_out, in_1[0]);
  and and_35 (and_35_out, not_1_out, in_1[2]);
  and and_36 (and_36_out, in_1[3], not_2_out);
  or or_1 (or_1_out, and_1_out, and_2_out, and_3_out, and_4_out, and_5_out);
  or or_2 (or_2_out, and_6_out, and_7_out, and_8_out, and_9_out, and_10_out);
  or or_3 (or_3_out, and_11_out, and_12_out, and_13_out, and_14_out, and_15_out, and_16_out);
  or or_4 (or_4_out, and_17_out, and_18_out, and_19_out, and_20_out, and_21_out);
  or or_5 (or_5_out, and_22_out, and_23_out, and_24_out, and_25_out, and_26_out);
  or or_6 (or_6_out, and_27_out, and_28_out, and_29_out, and_30_out, and_31_out);
  or or_7 (or_7_out, and_32_out, and_33_out, and_34_out, and_35_out, and_36_out);
  not not_5 (not_5_out, Kontrola_za_minus_i_greske);
  or or_8 (out_3[3], Kontrola_za_minus_i_greske, or_1_out);
  and and_37 (out_3[2], not_5_out, or_2_out);
  and and_38 (out_3[1], not_5_out, or_3_out);
  and and_39 (out_3[0], not_5_out, or_4_out);
  and and_40 (out_4[3], not_5_out, or_5_out);
  and and_41 (out_4[2], not_5_out, or_6_out);
  and and_42 (out_4[1], not_5_out, or_7_out);

  assign out_4[0] = 1'b0;
endmodule
