// Logisim project Vjezbe4.circ as structural Verilog: 1 circuit, main circuit main
module main (
  input  [3:0] A,
  input  [3:0] B,
  input  [2:0] SelOp,
  output [3:0] \Za_logičke_operacije 
);

  wire alu_1__2__ulaz_za_1__nbcd, alu_1__2__ulaz_za_2__nbcd, alu_1__2__ulaz_za_3__nbcd;
  wire [3:0] alu_1__1__ulaz_za_1__nbcd, alu_1__1__ulaz_za__3__nbcd, nbcd_1_out_3, nbcd_1_out_4, nbcd_2_out_3,
       nbcd_2_out_4, nbcd_3_out_3, nbcd_3_out_4, nbcd_4_out_3, nbcd_4_out_4, nbcd_5_out_3, nbcd_5_out_4;

  NBCD nbcd_1 (.out_3(nbcd_1_out_3), .out_4(nbcd_1_out_4), .in_1(A), .Kontrola_za_minus_i_greske(1'b0));
  NBCD nbcd_2 (.out_3(nbcd_2_out_3), .out_4(nbcd_2_out_4), .in_1(B), .Kontrola_za_minus_i_greske(1'b0));
  _7_Segment_Display u_7_segment_display_1 (
    .g(nbcd_1_out_3[3]), .f(nbcd_1_out_3[2]), .a(nbcd_1_out_3[1]), .b(nbcd_1_out_3[0]), .e(nbcd_1_out_4[3]),
    .d(nbcd_1_out_4[2]), .c(nbcd_1_out_4[1]), .dp(nbcd_1_out_4[0]));
  _7_Segment_Display u_7_segment_display_2 (
    .g(nbcd_2_out_3[3]), .f(nbcd_2_out_3[2]), .a(nbcd_2_out_3[1]), .b(nbcd_2_out_3[0]), .e(nbcd_2_out_4[3]),
    .d(nbcd_2_out_4[2]), .c(nbcd_2_out_4[1]), .dp(nbcd_2_out_4[0]));
  ALU alu_1 (
    .A(A), .B(B), .SelOp(SelOp), ._1__Ulaz_za__3__NBCD(alu_1__1__ulaz_za__3__nbcd),
    ._2__Ulaz_za_1__NBCD(alu_1__2__ulaz_za_1__nbcd), ._2__Ulaz_za_2__NBCD(alu_1__2__ulaz_za_2__nbcd),
    ._2__Ulaz_za_3__NBCD(alu_1__2__ulaz_za_3__nbcd), ._1__Ulaz_za_2_NBCD(\Za_logičke_operacije ),
    ._1__Ulaz_za_1__NBCD(alu_1__1__ulaz_za_1__nbcd));
  NBCD nbcd_3 (
    .out_3(nbcd_3_out_3), .out_4(nbcd_3_out_4), .in_1(alu_1__1__ulaz_za_1__nbcd),
    .Kontrola_za_minus_i_greske(alu_1__2__ulaz_za_1__nbcd));
  _7_Segment_Display u_7_segment_display_3 (
    .g(nbcd_3_out_3[3]), .f(nbcd_3_out_3[2]), .a(nbcd_3_out_3[1]), .b(nbcd_3_out_3[0]), .e(nbcd_3_out_4[3]),
    .d(nbcd_3_out_4[2]), .c(nbcd_3_out_4[1]), .dp(nbcd_3_out_4[0]));
  _7_Segment_Display u_7_segment_display_4 (
    .g(nbcd_4_out_3[3]), .f(nbcd_4_out_3[2]), .a(nbcd_4_out_3[1]), .b(nbcd_4_out_3[0]), .e(nbcd_4_out_4[3]),
    .d(nbcd_4_out_4[2]), .c(nbcd_4_out_4[1]), .dp(nbcd_4_out_4[0]));
  NBCD nbcd_4 (
    .out_3(nbcd_4_out_3), .out_4(nbcd_4_out_4), .in_1(alu_1__1__ulaz_za__3__nbcd),
    .Kontrola_za_minus_i_greske(alu_1__2__ulaz_za_3__nbcd));
  _7_Segment_Display u_7_segment_display_5 (
    .g(nbcd_5_out_3[3]), .f(nbcd_5_out_3[2]), .a(nbcd_5_out_3[1]), .b(nbcd_5_out_3[0]), .e(nbcd_5_out_4[3]),
    .d(nbcd_5_out_4[2]), .c(nbcd_5_out_4[1]), .dp(nbcd_5_out_4[0]));
  NBCD nbcd_5 (
    .out_3(nbcd_5_out_3), .out_4(nbcd_5_out_4), .in_1(\Za_logičke_operacije ),
    .Kontrola_za_minus_i_greske(alu_1__2__ulaz_za_2__nbcd));
endmodule
